# Fritzing sketch hookup_diagram_pi_led (saved by Fritzing 0.9.1b)
breadboards: 1

parts:
  LED1 = LEDs [package=led10mm]  # not connected
  LED1_2 = LEDs [package=led10mm]  # not connected
  LED1_3 = LEDs [package=led10mm]  # not connected
  R1 = Resistor [package="0402 [SMD]"]
  Raspberry_Pi1 = Raspberry Pi B rev2

nets:
  N1: R1.Pin_1, Raspberry_Pi1.GPIO_18
